# Fritzing sketch Arduino Based Social Distancing Alarm System (saved by Fritzing 0.9.3b)
breadboards: 1

parts:
  R1 = Resistor [tolerance=±5% resistance=220 package=THT]
  LED1 = LED - 5mm [color="Red (633nm)" package="5 mm [THT]"]
  J1 = Piezo Speaker
  R2 = Rotary Potentiometer (Large) [maximum_resistance=100kΩ package=THT]
  U1 = SWITCH_SPDT [package=kps-1290]
  U2 = LCD-16X2 [package=lcd-16x2]
  Part1 = Arduino Nano (Rev3.0)  # not connected
  U3 = LIPO-1000mAh [package=lipo-1000]
  hc-sr1 = hc-sr04
  R3 = Resistor [tolerance=±5% resistance=220 package=THT]
  LED2 = LED - 5mm [color="Red (633nm)" package="5 mm [THT]"]

nets:
  N1: R1.Pin_0, LED1.anode
  N2: LED1.cathode, J1.pin1, U3.-, hc-sr1.GND, LED2.cathode
  N3: R2.leg1, U2.VSS, U2.R_W, U2.K
  N4: R2.wiper, U2.VO
  N5: R2.leg2, U2.VDD, U2.A
  N6: U1.S, U3.+
  N7: R3.Pin_0, LED2.anode

notes:
  3.7V Lipo Battery
  SPDT switch
  Piezzo Buzzer
  220 ohm Resistor
  Red LED
  HC-SR04 UltraSonic Sensor
  Potentiometer 10K
  LCD 16x2
  Arduino Based Social Distancing Alarm System
  Made by : Rumil Christian T. Seloveres
  Course : Bachelor of Science in Computer Engineering
  Green LED
